// Logisim project Projekt 1.circ as structural Verilog: 1 circuit, main circuit main
module main (
  input  in_1,
  input  in_2,
  input  in_3,
  output out_4,
  output out_5,
  output out_6
);

  wire and_1_out, and_2_out, and_3_out, and_4_out, nand_1_out, nor_1_out, not_1_out, not_2_out, not_3_out,
       not_4_out, or_1_out, xor_1_out;

  not not_1 (not_1_out, in_3);
  not not_2 (not_2_out, in_1);
  and and_1 (and_1_out, in_1, not_1_out);
  nand nand_1 (nand_1_out, in_2, in_3);
  not not_3 (not_3_out, in_3);
  not not_4 (not_4_out, in_2);
  or or_1 (or_1_out, not_2_out, in_2);
  nor nor_1 (nor_1_out, in_2, and_1_out);
  and and_2 (and_2_out, in_1, nand_1_out);
  and and_3 (and_3_out, in_1, not_3_out);
  xor xor_1 (xor_1_out, not_4_out, 1'b0);
  and and_4 (and_4_out, or_1_out, nor_1_out);
  or or_2 (out_4, and_4_out, and_2_out);
  or or_3 (out_6, and_3_out, xor_1_out);
  Comparator #(.width(1), .mode("unsigned")) comparator_1 (.a(out_4), .b(out_6), .eq(out_5));  // open: gt, lt
endmodule
