// Logisim project Projekt 1_b.circ as structural Verilog: 1 circuit, main circuit main
module main (
  input  in_1,
  input  in_2,
  input  in_3,
  input  in_4,
  input  in_5,
  input  in_6,
  output out_7,
  output out_8,
  output out_9,
  output out_10,
  output out_11,
  output out_12
);

  and and_1 (out_7, in_1, in_2);
  not not_1 (out_9, in_3);
  xor xor_1 (out_8, in_2, in_3);
  // NOT_Gate not_2 is placed but not wired
  // AND_Gate and_2 is placed but not wired
  // XOR_Gate xor_2 is placed but not wired
endmodule
